// Logisim project PyGO.circ as structural Verilog: 8 circuits, main circuit PROCESSADOR
// Py-Go
module PROCESSADOR (
  input  [31:0] pulos,
  input  [31:0] mem_saida,
  input  Clock,
  output [31:0] \INSTRUÇÃO ,
  output out_5,
  output out_6,
  output [31:0] ula_saida,
  output [31:0] ula_volta,
  output mem_reset
);

  wire data_razard, Inst_reset, J, Jc, Li, li_r, marc, mine1_out, mine2_out, not_1_out, T_or_F, writ_reg;
  wire [1:0] register_9_q;
  wire [3:0] register_8_q, register_15_q, register_20_q;
  wire [7:0] register_3_q, UC_ula_op;
  wire [23:0] register_18_q;
  wire [31:0] adder_1_out, auxiliar_do_branch_1_out_5, banco_de_registradores_1_r1_d, multiplexer_1_out,
       multiplexer_2_out, multiplexer_3_out, PC_q, R0D, redutor_1_out_2, register_1_q, register_4_q,
       register_5_q, register_6_q, register_7_q, register_10_q, register_11_q, register_12_q, register_13_q,
       register_19_q, rom_1_data, ULA, ula_1_ula_out;
  wire [31:24] register_18_q_2;

  Multiplexer #(.width(32), .enable("false")) multiplexer_1 (
    .in0(adder_1_out), .in1(register_10_q), .out(multiplexer_1_out), .sel(marc));
  Button button_1 (.out(Inst_reset));
  Register #(.width(32)) PC (.D(multiplexer_1_out), .Q(PC_q), .clk(Clock), .clr(Inst_reset));  // open: en
  Adder #(.width(32)) adder_1 (.a(pulos), .b(PC_q), .out(adder_1_out));  // open: cin, cout
  ROM #(.dataWidth(32)) rom_1 (.addr(PC_q[9:2]), .data(rom_1_data));  // open: sel
  Register #(.width(32)) register_1 (.D(adder_1_out), .Q(register_1_q), .clk(Clock), .clr(Inst_reset));  // open: en
  Register #(.width(32)) register_2 (.D(rom_1_data), .Q(\INSTRUÇÃO ), .clk(Clock), .clr(Inst_reset));  // open: en
  UC UC (
    .E3(\INSTRUÇÃO [31]), .E2(\INSTRUÇÃO [30]), .ula_op(UC_ula_op[0]), .E1(\INSTRUÇÃO [29]),
    .E0(\INSTRUÇÃO [28]), .ula_r(UC_ula_op[1]), .write_reg(UC_ula_op[2]), .li(UC_ula_op[3]),
    .j(UC_ula_op[4]), .branch(UC_ula_op[5]), .MemRead(UC_ula_op[6]), .MemWrite(UC_ula_op[7]),
    .datarazard(data_razard));
  BANCO_DE_REGISTRADORES banco_de_registradores_1 (
    .DATA_WRITE(multiplexer_3_out), .CLK(Clock), .RW(register_20_q), .R0_D(R0D), .R0(\INSTRUÇÃO [19:16]),
    .R1_D(banco_de_registradores_1_r1_d), .R1(\INSTRUÇÃO [23:20]), .RW_2(writ_reg), .RESET(Inst_reset));
  Multiplexer #(.width(32), .enable("false")) multiplexer_2 (
    .in0(R0D), .in1(ULA), .out(multiplexer_2_out), .sel(data_razard));
  Multiplexer #(.width(32), .enable("false")) multiplexer_3 (
    .in0(register_19_q), .in1({{8{1'b0}}, register_18_q}), .out(multiplexer_3_out), .sel(Li));
  Register register_3 (
    .D(UC_ula_op), .Q({register_3_q[7:5], J, li_r, register_3_q[2:0]}), .clk(Clock), .clr(Inst_reset));  // open: en
  Register #(.width(32)) register_4 (.D(\INSTRUÇÃO ), .Q(register_4_q), .clk(Clock), .clr(Inst_reset));  // open: en
  Register #(.width(32)) register_5 (.D(\INSTRUÇÃO ), .Q(register_5_q), .clk(Clock), .clr(Inst_reset));  // open: en
  Register #(.width(32)) register_6 (
    .D(multiplexer_2_out), .Q(register_6_q), .clk(Clock), .clr(Inst_reset));  // open: en
  Register #(.width(32)) register_7 (
    .D(banco_de_registradores_1_r1_d), .Q(register_7_q), .clk(Clock), .clr(Inst_reset));  // open: en
  Register #(.width(4)) register_8 (
    .D(\INSTRUÇÃO [27:24]), .Q(register_8_q), .clk(Clock), .clr(Inst_reset));  // open: en
  auxiliar_do_branch auxiliar_do_branch_1 (
    .Normal(register_1_q), .Sem_soma(register_5_q), .in_3(Jc), .j(J), .out_5(auxiliar_do_branch_1_out_5));
  and and_1 (Jc, register_3_q[5], T_or_F);
  ULA ula_1 (
    .DATA_0(register_6_q), .DATA_1(register_7_q), .ULA_OUT(ula_1_ula_out), .ULA_OP(register_3_q[1:0]),
    .out_6(T_or_F), .clk(Clock));
  REDUTOR redutor_1 (.out_2(redutor_1_out_2), .in_1(register_4_q));
  Multiplexer #(.width(32), .enable("false")) multiplexer_4 (
    .in0(redutor_1_out_2), .in1(ula_1_ula_out), .out(ULA), .sel(not_1_out));
  not not_1 (not_1_out, li_r);
  or mine1 (mine1_out, Jc, J);
  Register #(.width(4)) register_9 (
    .D({register_3_q[7:6], li_r, register_3_q[2]}), .Q({out_5, out_6, register_9_q}), .clk(Clock),
    .clr(Inst_reset));  // open: en
  Register #(.width(32)) register_10 (
    .D(auxiliar_do_branch_1_out_5), .Q(register_10_q), .clk(Clock), .clr(Inst_reset));  // open: en
  Register #(.width(32)) register_11 (.D(register_4_q), .Q(register_11_q), .clk(Clock), .clr(Inst_reset));  // open: en
  Register #(.width(32)) register_12 (.D(register_6_q), .Q(register_12_q), .clk(Clock), .clr(Inst_reset));  // open: en
  Register #(.width(32)) register_13 (.D(ula_1_ula_out), .Q(register_13_q), .clk(Clock), .clr(Inst_reset));  // open: en
  Register #(.width(32)) register_14 (.D(register_7_q), .Q(ula_volta), .clk(Clock), .clr(Inst_reset));  // open: en
  Register #(.width(4)) register_15 (.D(register_8_q), .Q(register_15_q), .clk(Clock), .clr(Inst_reset));  // open: en
  Register #(.width(1)) register_16 (.D(mine1_out), .Q(marc), .clk(Clock), .clr(Inst_reset));  // open: en
  Multiplexer #(.width(32), .enable("false")) multiplexer_5 (
    .in0(register_12_q), .in1(register_13_q), .out(ula_saida), .sel(mine2_out));
  nor mine2 (mine2_out, out_5, out_6);
  Register #(.width(2)) register_17 (.D(register_9_q), .Q({Li, writ_reg}), .clk(Clock), .clr(Inst_reset));  // open: en
  Register #(.width(32)) register_18 (
    .D(register_11_q), .Q({register_18_q_2, register_18_q}), .clk(Clock), .clr(Inst_reset));  // open: en
  Register #(.width(32)) register_19 (.D(mem_saida), .Q(register_19_q), .clk(Clock), .clr(Inst_reset));  // open: en
  Register #(.width(4)) register_20 (.D(register_15_q), .Q(register_20_q), .clk(Clock), .clr(Inst_reset));  // open: en

  // Notes on the sheet:
  //   contents of rom_1 (hex, n*v repeats v):
  //   23000004 24000000 25000001 20000000 21000010 22000020 6043001a 26000000 4*b0000000 6063000e b0000000
  //   b0000000 a7000000 a8000000 49340000 c9600000 ca000000 f0700000 b0000000 b0000000 b910000 f0800000
  //   6560000 3000000c 4*b0000000 4540000 30000006 4*b0000000 24000000 4*b0000000 6043002f 26000000
  //   4*b0000000 60630022 27000000 b0000000 b0000000 b0000000 28000000 60630012 b0000000 b0000000 b0000000
  //   49340000 c9700000 c9000000 e9000000 4a370000 ca600000 ca100000 ea000000 b0000000 b0000000 b0000000
  //   7570000 49a90000 c8800000 30000036 4*b0000000 49340000 c9600000 c9200000 f0800000 6560000 30000030
  //   4*b0000000 4540000 3000002a 4*b0000000
  //   REG_0
  //   REG_1
  //   REG_W
  //   DATA_W
  //   BANCO DE REGISTRADORES
  //   REG0_D
  //   ULA
endmodule

module ULA (
  input  [31:0] DATA_0,
  input  [31:0] DATA_1,
  input  [1:0] ULA_OP,
  input  clk,
  output [31:0] ULA_OUT,
  output out_6
);

  wire comparator_1_eq, comparator_1_gt, comparator_1_lt;
  wire [6:0] random_1_out;
  wire [31:0] adder_1_out, multiplier_1_out, subtractor_1_out;

  Adder #(.width(32)) adder_1 (.a(DATA_0), .b(DATA_1), .out(adder_1_out));  // open: cin, cout
  Subtractor #(.width(32)) subtractor_1 (.a(DATA_0), .b(DATA_1), .out(subtractor_1_out));  // open: bin, bout
  Multiplier #(.width(32)) multiplier_1 (.a(DATA_0), .b(DATA_1), .out(multiplier_1_out));  // open: cin, cout
  Comparator #(.width(32), .mode("unsigned")) comparator_1 (
    .a(DATA_0), .b(DATA_1), .gt(comparator_1_gt), .eq(comparator_1_eq), .lt(comparator_1_lt));
  Random #(.width(7)) random_1 (.clk(clk), .out(random_1_out));  // open: next, clr
  Multiplexer #(.select(2), .width(32), .enable("false")) multiplexer_1 (
    .in0(adder_1_out), .in1(subtractor_1_out), .in2(multiplier_1_out), .in3({{25{1'b0}}, random_1_out}),
    .out(ULA_OUT), .sel(ULA_OP));
  Multiplexer #(.select(2), .enable("false")) multiplexer_2 (
    .in0(comparator_1_gt), .in1(comparator_1_eq), .in2(comparator_1_lt), .in3(1'b0), .out(out_6), .sel(ULA_OP));
endmodule

module UC (
  input  E3,
  input  E2,
  input  E1,
  input  E0,
  output ula_op,
  output ula_r,
  output write_reg,
  output li,
  output j,
  output branch,
  output MemRead,
  output MemWrite,
  output datarazard
);

  wire and_1_out, and_2_out, and_3_out, and_4_out, and_5_out, and_6_out, and_7_out, and_9_out, and_10_out,
       and_11_out, and_12_out, and_13_out, and_14_out, and_15_out, and_18_out, and_19_out, and_20_out,
       and_21_out, not_1_out, not_2_out, not_3_out, not_4_out, not_5_out, not_6_out, not_7_out, not_8_out,
       not_9_out, not_10_out, not_11_out, not_12_out, not_13_out, not_14_out, not_15_out, not_16_out,
       not_17_out, not_18_out, not_19_out, not_20_out, not_21_out, not_22_out, not_23_out, not_24_out,
       not_25_out, not_26_out, not_27_out, not_28_out, not_29_out, not_30_out, not_31_out, not_32_out,
       not_33_out, not_34_out, not_35_out;

  not not_1 (not_1_out, E2);
  not not_2 (not_2_out, E1);
  not not_3 (not_3_out, E3);
  not not_4 (not_4_out, E0);
  not not_5 (not_5_out, E2);
  not not_6 (not_6_out, E0);
  not not_7 (not_7_out, E3);
  not not_8 (not_8_out, E1);
  not not_9 (not_9_out, E0);
  not not_10 (not_10_out, E3);
  not not_11 (not_11_out, E2);
  not not_12 (not_12_out, E0);
  not not_13 (not_13_out, E1);
  not not_14 (not_14_out, E3);
  not not_15 (not_15_out, E2);
  and and_1 (and_1_out, not_14_out, not_15_out, not_16_out);
  not not_16 (not_16_out, E1);
  not not_17 (not_17_out, E2);
  and and_2 (and_2_out, not_17_out, not_18_out);
  not not_18 (not_18_out, E0);
  not not_19 (not_19_out, E1);
  and and_3 (and_3_out, not_19_out, not_20_out);
  not not_20 (not_20_out, E0);
  and and_4 (and_4_out, E3, not_21_out);
  not not_21 (not_21_out, E0);
  and and_5 (and_5_out, E3, E2, not_22_out);
  not not_22 (not_22_out, E1);
  not not_23 (not_23_out, E3);
  not not_24 (not_24_out, E2);
  not not_25 (not_25_out, E0);
  not not_26 (not_26_out, E3);
  not not_27 (not_27_out, E2);
  not not_28 (not_28_out, E3);
  and and_6 (and_6_out, not_28_out, E2, E0);
  not not_29 (not_29_out, E3);
  and and_7 (and_7_out, not_29_out, E2, E1);
  not not_30 (not_30_out, E2);
  not not_31 (not_31_out, E1);
  not not_32 (not_32_out, E0);
  not not_33 (not_33_out, E0);
  not not_34 (not_34_out, E2);
  not not_35 (not_35_out, E1);
  and and_8 (datarazard, E3, E2);
  and and_9 (and_9_out, not_1_out, not_2_out, E0);
  and and_10 (and_10_out, not_3_out, E2, E1, not_4_out);
  or or_1 (ula_op, and_9_out, and_10_out, and_11_out);
  and and_11 (and_11_out, E3, not_5_out, E1, not_6_out);
  and and_12 (and_12_out, not_7_out, E2, not_8_out, not_9_out);
  and and_13 (and_13_out, not_10_out, E2, E1, E0);
  and and_14 (and_14_out, E3, not_11_out, E1, not_12_out);
  and and_15 (and_15_out, E3, E2, not_13_out, E0);
  or or_2 (write_reg, and_1_out, and_2_out, and_3_out, and_4_out, and_5_out);
  and and_16 (li, not_23_out, not_24_out, E1, not_25_out);
  and and_17 (j, not_26_out, not_27_out, E1, E0);
  or or_3 (branch, and_6_out, and_7_out);
  and and_18 (and_18_out, E3, not_30_out, not_31_out, not_32_out);
  or or_4 (MemRead, and_18_out, and_19_out);
  and and_19 (and_19_out, E3, E2, E1, not_33_out);
  and and_20 (and_20_out, E3, not_34_out, not_35_out, E0);
  or or_5 (MemWrite, and_20_out, and_21_out);
  and and_21 (and_21_out, E3, E2, E1, E0);
  or or_6 (ula_r, and_12_out, and_13_out, and_14_out, and_15_out);
endmodule

module BANCO_DE_REGISTRADORES (
  input  [31:0] DATA_WRITE,
  input  [3:0] R0,
  input  [3:0] R1,
  input  [3:0] RW,
  input  CLK,
  input  RESET,
  input  RW_2,
  output [31:0] R0_D,
  output [31:0] R1_D
);

  wire demultiplexer_1_out0, demultiplexer_1_out1, demultiplexer_1_out2, demultiplexer_1_out3,
       demultiplexer_1_out4, demultiplexer_1_out5, demultiplexer_1_out6, demultiplexer_1_out7,
       demultiplexer_1_out8, demultiplexer_1_out9, demultiplexer_1_out10, demultiplexer_1_out11,
       demultiplexer_1_out12, demultiplexer_1_out13, demultiplexer_1_out14, demultiplexer_1_out15;
  wire [31:0] register_1_q, register_2_q, register_3_q, register_4_q, register_5_q, register_6_q,
       register_7_q, register_8_q, register_9_q, register_10_q, register_11_q, register_12_q, register_13_q,
       register_14_q, register_15_q, register_16_q;

  Demultiplexer #(.select(4)) demultiplexer_1 (
    .out0(demultiplexer_1_out0), .out1(demultiplexer_1_out1), .out2(demultiplexer_1_out2),
    .out3(demultiplexer_1_out3), .out4(demultiplexer_1_out4), .out5(demultiplexer_1_out5),
    .out6(demultiplexer_1_out6), .out7(demultiplexer_1_out7), .out8(demultiplexer_1_out8),
    .out9(demultiplexer_1_out9), .out10(demultiplexer_1_out10), .out11(demultiplexer_1_out11),
    .out12(demultiplexer_1_out12), .out13(demultiplexer_1_out13), .out14(demultiplexer_1_out14),
    .out15(demultiplexer_1_out15), .in(RW_2), .sel(RW));  // open: en
  Register #(.width(32)) register_1 (
    .D(DATA_WRITE), .en(demultiplexer_1_out0), .Q(register_1_q), .clk(CLK), .clr(RESET));
  Register #(.width(32)) register_2 (
    .D(DATA_WRITE), .en(demultiplexer_1_out1), .Q(register_2_q), .clk(CLK), .clr(RESET));
  Register #(.width(32)) register_3 (
    .D(DATA_WRITE), .en(demultiplexer_1_out2), .Q(register_3_q), .clk(CLK), .clr(RESET));
  Register #(.width(32)) register_4 (
    .D(DATA_WRITE), .en(demultiplexer_1_out3), .Q(register_4_q), .clk(CLK), .clr(RESET));
  Register #(.width(32)) register_5 (
    .D(DATA_WRITE), .en(demultiplexer_1_out4), .Q(register_5_q), .clk(CLK), .clr(RESET));
  Register #(.width(32)) register_6 (
    .D(DATA_WRITE), .en(demultiplexer_1_out5), .Q(register_6_q), .clk(CLK), .clr(RESET));
  Register #(.width(32)) register_7 (
    .D(DATA_WRITE), .en(demultiplexer_1_out6), .Q(register_7_q), .clk(CLK), .clr(RESET));
  Register #(.width(32)) register_8 (
    .D(DATA_WRITE), .en(demultiplexer_1_out7), .Q(register_8_q), .clk(CLK), .clr(RESET));
  Register #(.width(32)) register_9 (
    .D(DATA_WRITE), .en(demultiplexer_1_out8), .Q(register_9_q), .clk(CLK), .clr(RESET));
  Register #(.width(32)) register_10 (
    .D(DATA_WRITE), .en(demultiplexer_1_out9), .Q(register_10_q), .clk(CLK), .clr(RESET));
  Register #(.width(32)) register_11 (
    .D(DATA_WRITE), .en(demultiplexer_1_out10), .Q(register_11_q), .clk(CLK), .clr(RESET));
  Register #(.width(32)) register_12 (
    .D(DATA_WRITE), .en(demultiplexer_1_out11), .Q(register_12_q), .clk(CLK), .clr(RESET));
  Register #(.width(32)) register_13 (
    .D(DATA_WRITE), .en(demultiplexer_1_out12), .Q(register_13_q), .clk(CLK), .clr(RESET));
  Register #(.width(32)) register_14 (
    .D(DATA_WRITE), .en(demultiplexer_1_out13), .Q(register_14_q), .clk(CLK), .clr(RESET));
  Register #(.width(32)) register_15 (
    .D(DATA_WRITE), .en(demultiplexer_1_out14), .Q(register_15_q), .clk(CLK), .clr(RESET));
  Register #(.width(32)) register_16 (
    .D(DATA_WRITE), .en(demultiplexer_1_out15), .Q(register_16_q), .clk(CLK), .clr(RESET));
  Multiplexer #(.select(4), .width(32), .disabled(0), .enable("false")) multiplexer_1 (
    .in0(register_1_q), .in1(register_2_q), .in2(register_3_q), .in3(register_4_q), .in4(register_5_q),
    .in5(register_6_q), .in6(register_7_q), .in7(register_8_q), .in8(register_9_q), .in9(register_10_q),
    .in10(register_11_q), .in11(register_12_q), .in12(register_13_q), .in13(register_14_q),
    .in14(register_15_q), .in15(register_16_q), .out(R0_D), .sel(R0));
  Multiplexer #(.select(4), .width(32), .enable("false")) multiplexer_2 (
    .in0(register_1_q), .in1(register_2_q), .in2(register_3_q), .in3(register_4_q), .in4(register_5_q),
    .in5(register_6_q), .in6(register_7_q), .in7(register_8_q), .in8(register_9_q), .in9(register_10_q),
    .in10(register_11_q), .in11(register_12_q), .in12(register_13_q), .in13(register_14_q),
    .in14(register_15_q), .in15(register_16_q), .out(R1_D), .sel(R1));

  // Other names for the same wires on the sheet: In[31:0] = DATA_WRITE; R = RESET
endmodule

// auxiliar
module auxiliar_do_branch (
  input  [31:0] Normal,
  input  [31:0] Sem_soma,
  input  in_3,
  input  j,
  output [31:0] out_5
);

  wire [31:0] adder_1_out, multiplexer_1_out;

  Adder #(.width(32)) adder_1 (
    .a({{9{1'b0}}, Sem_soma[20:0], 2'b00}), .b(Normal), .out(adder_1_out));  // open: cin, cout
  Multiplexer #(.width(32), .enable("false")) multiplexer_1 (
    .in0(Normal), .in1(adder_1_out), .out(multiplexer_1_out), .sel(in_3));
  Multiplexer #(.width(32), .enable("false")) multiplexer_2 (
    .in0(multiplexer_1_out), .in1({2'b00, Sem_soma[27:0], 2'b00}), .out(out_5), .sel(j));
endmodule

// Data Memory
module data_memory (
  input  [31:0] in_1,
  input  MemRead,
  input  [31:0] in_3,
  input  clk,
  input  MemWrite,
  input  limpa,
  output [31:0] out_7
);

  wire [31:0] ram_1_data;

  RAM #(.addrWidth(24), .dataWidth(32), .bus("separate")) ram_1 (
    .addr(in_1[23:0]), .din(in_3), .data(ram_1_data), .str(MemWrite), .clk(clk), .clr(limpa));  // open: sel, ld
  Multiplexer #(.width(32), .enable("false")) multiplexer_1 (.in0(in_1), .in1(ram_1_data), .out(out_7), .sel(MemRead));
endmodule

module REDUTOR (
  input  [31:0] in_1,
  output [31:0] out_2
);


  assign out_2 = {{8{1'b0}}, in_1[23:0]};
endmodule

module Pro_PyGo (
);

  wire button_1_out, clock_1_out;
  wire [31:0] processador_1_ula_saida;

  Clock clock_1 (.out(clock_1_out));
  Button button_1 (.out(button_1_out));
  PROCESSADOR processador_1 (
    .Clock(clock_1_out), .mem_reset(button_1_out), .ula_saida(processador_1_ula_saida));  // open: pulos, mem_saida, INSTRUÇÃO, out_5, out_6, ula_volta
  PROCESSADOR processador_2 (
    .Clock(clock_1_out), .mem_reset(button_1_out));  // open: pulos, mem_saida, INSTRUÇÃO, out_5, out_6, ula_saida, ula_volta
  Multiplexer #(.width(5)) multiplexer_1 ();  // open: in0, in1, out, sel, en
  data_memory data_memory_1 (.in_1(processador_1_ula_saida));  // open: in_3, MemWrite, out_7, clk, MemRead, limpa
endmodule
